# Fritzing sketch Buzzer (saved by Fritzing 0.9.10b)
breadboards: 1

parts:
  V1 = DC Power [voltage=5]
  Mod1 = Amica NodeMCU DEVKIT 1.0
  Mod2 = Passive Buzzer

nets:
  N1: V1.V-, Mod1.pin2, Mod1.pin_9, Mod2.-
  N2: Mod1.pin1, Mod1.pin_10, Mod2.NC
  N3: Mod1.pin8, Mod2.S
